// Digital circuit ALUREGS.dig as structural Verilog
module ALUREGS (
  input  clk
);

  wire add_1_c_o, and_1_out, and_2_out, counter_1_ovf, counterpreset_1_ovf, decoder_1_out_2, decoder_1_out_3,
       decoder_1_out_4, not_1_out, or_1_out, or_2_out;
  wire [2:0] counter_1_out;
  wire [3:0] add_1_s, add_2_s, counterpreset_1_out, eeprom_1_d, Left_q, multiplexer_1_out, multiplexer_2_out,
       multiplexer_3_out, multiplexer_4_out, Right_nq, Right_q;

  Counter #(.Bits(3)) counter_1 (.en(1'b1), .C(clk), .clr(counter_1_ovf), .out(counter_1_out), .ovf(counter_1_ovf));
  CounterPreset #(.Bits(4)) counterpreset_1 (
    .en(1'b1), .C(counter_1_ovf), .dir(1'b0), .in(4'b0000), .ld(1'b0), .clr(counterpreset_1_ovf),
    .out(counterpreset_1_out), .ovf(counterpreset_1_ovf));
  Multiplexer #(.Bits(4)) multiplexer_1 (
    .sel(decoder_1_out_3), .in_0(4'b0000), .in_1(4'b0001), .out(multiplexer_1_out));
  Decoder #(.Selector_Bits(3)) decoder_1 (
    .sel(counter_1_out), .out_2(decoder_1_out_2), .out_3(decoder_1_out_3), .out_4(decoder_1_out_4));  // open: out_0, out_1, out_5, out_6, out_7
  Seven_Seg_Hex seven_seg_hex_1 (.d(counterpreset_1_out), .dp(1'b0));
  not not_1 (not_1_out, counter_1_out[2]);
  EEPROM #(.AddrBits(8), .Bits(4)) eeprom_1 (
    .A({multiplexer_1_out, counterpreset_1_out}), .CS(1'b1), .WE(decoder_1_out_4), .OE(not_1_out),
    .D(eeprom_1_d));
  Seven_Seg_Hex seven_seg_hex_2 (.d(eeprom_1_d), .dp(1'b0));
  assign eeprom_1_d = decoder_1_out_4 ? multiplexer_2_out : 4'bz;  // Driver driver_1
  D_FF #(.Bits(4)) Left (.D(eeprom_1_d), .C(decoder_1_out_2), .Q(Left_q));  // open: nQ
  D_FF #(.Bits(4)) Right (.D(eeprom_1_d), .C(decoder_1_out_3), .Q(Right_q), .nQ(Right_nq));
  Multiplexer #(.Selector_Bits(2), .Bits(4)) multiplexer_2 (
    .sel(2'b00), .in_0(add_2_s), .in_1(add_2_s), .in_2(Left_q), .in_3(Right_q), .out(multiplexer_2_out));
  Multiplexer #(.Bits(4)) multiplexer_3 (.sel(1'b0), .in_0(Right_q), .in_1(Right_nq), .out(multiplexer_3_out));
  Add #(.Bits(4)) add_1 (.a(Left_q), .b(multiplexer_3_out), .c_i(1'b0), .s(add_1_s), .c_o(add_1_c_o));
  Multiplexer #(.Bits(4)) multiplexer_4 (.sel(or_1_out), .in_0(4'b0000), .in_1(4'b0110), .out(multiplexer_4_out));
  or or_1 (or_1_out, add_1_c_o, or_2_out);
  Add #(.Bits(4)) add_2 (.a(add_1_s), .b(multiplexer_4_out), .c_i(1'b0), .s(add_2_s));  // open: c_o
  and and_1 (and_1_out, add_1_s[1], add_1_s[3]);
  and and_2 (and_2_out, add_1_s[2], add_1_s[3]);
  or or_2 (or_2_out, and_1_out, and_2_out);

  // Notes on the sheet:
  //   contents of eeprom_1 (hex, n*v repeats v):
  //   3,4,5,6,7,8,9,0,1,0,0,0,0,0,0,0,4,9,9,9,9,9,9,9,9,9,9,9,9,9
endmodule
